// Logisim project 74194_3.circ as structural Verilog: 5 circuits, main circuit 74194
module _74194 (
  input  SL,
  input  A,
  input  B,
  input  C,
  input  D,
  input  S0,
  input  S1,
  input  SR,
  input  CLK,
  input  CLR,
  output QA,
  output QB,
  output QC,
  output QD
);

  wire and_1_out, and_2_out, and_3_out, and_4_out, and_5_out, and_6_out, and_7_out, and_8_out, and_9_out,
       and_10_out, and_11_out, and_12_out, and_13_out, nor_1_out, nor_2_out, nor_3_out, nor_4_out, nor_5_out,
       nor_6_out, not_1_out, not_2_out, not_3_out, not_4_out, not_5_out, not_6_out;

  not not_1 (not_1_out, S0);
  not not_2 (not_2_out, S1);
  nor nor_1 (nor_1_out, not_1_out, not_2_out);
  and and_1 (and_1_out, not_2_out, not_1_out);
  and and_2 (and_2_out, nor_1_out, A);
  and and_3 (and_3_out, SR, not_2_out);
  nor nor_2 (nor_2_out, and_3_out, and_2_out, and_4_out);
  nor nor_3 (nor_3_out, and_1_out, CLK);
  and and_4 (and_4_out, not_1_out, QB);
  not not_3 (not_3_out, nor_2_out);
  S_R_Flip_Flop s_r_ff_1 (.S(not_3_out), .clk(nor_3_out), .R(nor_2_out), .Q(QA), .reset(CLR));  // open: Qn, preset, en
  and and_5 (and_5_out, QA, not_2_out);
  and and_6 (and_6_out, not_1_out, QC);
  and and_7 (and_7_out, nor_1_out, B);
  nor nor_4 (nor_4_out, and_5_out, and_7_out, and_6_out);
  not not_4 (not_4_out, nor_4_out);
  S_R_Flip_Flop s_r_ff_2 (.S(not_4_out), .clk(nor_3_out), .R(nor_4_out), .Q(QB), .reset(CLR));  // open: Qn, preset, en
  and and_8 (and_8_out, nor_1_out, C);
  and and_9 (and_9_out, QB, not_2_out);
  nor nor_5 (nor_5_out, and_9_out, and_8_out, and_10_out);
  and and_10 (and_10_out, not_1_out, QD);
  not not_5 (not_5_out, nor_5_out);
  S_R_Flip_Flop s_r_ff_3 (.S(not_5_out), .clk(nor_3_out), .R(nor_5_out), .Q(QC), .reset(CLR));  // open: Qn, preset, en
  and and_11 (and_11_out, QC, not_2_out);
  and and_12 (and_12_out, nor_1_out, D);
  and and_13 (and_13_out, not_1_out, SL);
  nor nor_6 (nor_6_out, and_11_out, and_12_out, and_13_out);
  not not_6 (not_6_out, nor_6_out);
  S_R_Flip_Flop s_r_ff_4 (.S(not_6_out), .clk(nor_3_out), .R(nor_6_out), .Q(QD), .reset(CLR));  // open: Qn, preset, en
endmodule

module a (
  input  in_1,
  input  reset,
  output D,
  output C,
  output B,
  output A
);

  wire CLK_out, not_1_out;

  not not_1 (not_1_out, in_1);
  Clock CLK (.out(CLK_out));
  _74194 u_74194_1 (
    .S0(reset), .S1(in_1), .CLR(not_1_out), .SL(A), .A(1'b0), .B(1'b0), .C(1'b0), .D(in_1), .QB(B), .QC(C),
    .QD(D), .QA(A), .CLK(CLK_out));  // open: SR
endmodule

module b (
  input  CLR_S1,
  output QD,
  output QC,
  output QB,
  output QA
);

  wire CLK_out, nand_1_out, not_1_out;

  not not_1 (not_1_out, CLR_S1);
  Clock CLK (.out(CLK_out));
  _74194 u_74194_1 (
    .S0(1'b0), .S1(CLR_S1), .CLR(not_1_out), .SL(nand_1_out), .QB(QB), .QC(QC), .QD(QD), .QA(QA),
    .CLK(CLK_out));  // open: A, B, C, D, SR
  nand nand_1 (nand_1_out, QB, QC, QD);
endmodule

module c (
  input  in_1,
  output QD,
  output QC,
  output QB,
  output QA
);

  wire CLK_out, not_1_out;

  _74194 u_74194_1 (
    .S0(1'b0), .S1(in_1), .SL(not_1_out), .QB(QB), .QC(QC), .QD(QD), .QA(QA), .CLK(CLK_out));  // open: CLR, A, B, C, D, SR
  not not_1 (not_1_out, QA);
  Clock CLK (.out(CLK_out));
endmodule

module withShift (
  input  in_1,
  input  in_2,
  input  in_3,
  input  in_4,
  input  in_5,
  input  in_6,
  input  in_7,
  input  SR,
  input  CLR,
  output A,
  output B,
  output C,
  output D
);

  wire and_1_out, and_2_out, and_3_out, clock_1_out, shift_register_1_q0, shift_register_1_q1,
       shift_register_1_q2, shift_register_1_q3, shift_register_2_q0, shift_register_2_q1,
       shift_register_2_q2, shift_register_2_q3;

  or or_1 (A, shift_register_2_q3, shift_register_1_q0);
  or or_2 (B, shift_register_1_q1, shift_register_2_q2);
  or or_3 (C, shift_register_1_q2, shift_register_2_q1);
  or or_4 (D, shift_register_1_q3, shift_register_2_q0);
  and and_1 (and_1_out, in_1, in_2);
  and and_2 (and_2_out, in_1, SR);
  Clock clock_1 (.out(clock_1_out));
  Shift_Register #(.length(4), .trigger("falling")) shift_register_1 (
    .in(and_2_out), .clk(clock_1_out), .load(and_1_out), .clr(CLR), .d0(in_4), .q0(shift_register_1_q0),
    .d1(in_5), .q1(shift_register_1_q1), .d2(in_6), .q2(shift_register_1_q2), .d3(in_7),
    .q3(shift_register_1_q3));  // open: shift, out
  and and_3 (and_3_out, in_2, in_3);
  Shift_Register #(.length(4), .trigger("falling")) shift_register_2 (
    .in(and_3_out), .clk(clock_1_out), .clr(CLR), .q0(shift_register_2_q0), .q1(shift_register_2_q1),
    .q2(shift_register_2_q2), .q3(shift_register_2_q3));  // open: shift, out, load, d0, d1, d2, d3
endmodule
