// Logisim project Cwiczenia0.circ as structural Verilog: 1 circuit, main circuit main
module main (
  input  A,
  input  B,
  input  C,
  input  in_4,
  input  in_5,
  input  in_6,
  input  in_7,
  output out_8,
  output out_9,
  output out_10,
  output out_11
);

  wire AB_out, ABC_out, and_1_out, and_2_out, and_3_out, and_4_out, BC_out, d_ff_1_q, d_ff_1_qn, d_ff_2_q,
       d_ff_2_qn, d_ff_3_q, d_ff_3_qn, nand_1_out, nand_2_out, nand_3_out, nand_4_out, or_3_out, xor_1_out;

  D_Flip_Flop #(.trigger("falling")) d_ff_1 (
    .clk(in_4), .D(d_ff_1_qn), .Q(d_ff_1_q), .Qn(d_ff_1_qn));  // open: preset, en, reset
  D_Flip_Flop #(.trigger("falling")) d_ff_2 (
    .clk(d_ff_1_q), .D(d_ff_2_qn), .Q(d_ff_2_q), .Qn(d_ff_2_qn));  // open: preset, en, reset
  xor xor_1 (xor_1_out, in_5, in_6);
  D_Flip_Flop #(.trigger("falling")) d_ff_3 (
    .clk(d_ff_2_q), .D(d_ff_3_qn), .Q(d_ff_3_q), .Qn(d_ff_3_qn));  // open: preset, en, reset
  and and_1 (and_1_out, in_7, xor_1_out);
  and and_2 (and_2_out, in_5, in_5);
  xor xor_2 (out_10, xor_1_out, in_7);
  or or_1 (out_11, and_1_out, and_2_out);
  and AB (AB_out, A, B);
  and BC (BC_out, B, C);
  and ABC (ABC_out, C, B, A);
  and and_3 (and_3_out, d_ff_1_q, ~d_ff_2_q);  // AND_Gate
  and and_4 (and_4_out, d_ff_2_q, d_ff_3_q);
  nand nand_1 (nand_1_out, d_ff_2_q, d_ff_2_q);
  nand nand_2 (nand_2_out, d_ff_2_q, d_ff_3_q);
  nand nand_3 (nand_3_out, d_ff_1_q, nand_1_out);
  or or_2 (out_8, AB_out, ABC_out);
  or or_3 (or_3_out, and_3_out, and_4_out);
  nand nand_4 (nand_4_out, nand_3_out, nand_2_out);
  xor xor_3 (out_9, or_3_out, nand_4_out);

  // Notes on the sheet:
  //   a
  //   c
  //   b
  //   a
  //   c
  //   b
  //   AB+BC+ABC
endmodule
