// Logisim project Cwiczenia1.circ as structural Verilog: 4 circuits, main circuit 74194
module _74194 (
  input  A,
  input  B,
  input  C,
  input  D,
  input  SL,
  input  S0,
  input  S1,
  input  SR,
  input  CLK,
  input  CLR,
  output QA,
  output QB,
  output QC,
  output QD
);

  wire and_1_out, and_2_out, and_3_out, and_4_out, and_5_out, and_6_out, and_7_out, and_8_out, and_9_out,
       and_10_out, and_11_out, and_12_out, and_13_out, and_14_out, and_15_out, and_16_out, not_1_out,
       not_2_out, not_3_out, not_4_out, not_5_out, or_1_out, or_2_out, or_3_out, or_4_out;

  not not_1 (not_1_out, S0);
  not not_2 (not_2_out, S1);
  not not_3 (not_3_out, CLK);
  not not_4 (not_4_out, not_1_out);
  not not_5 (not_5_out, not_2_out);
  and and_1 (and_1_out, SR, not_1_out, not_5_out);
  and and_2 (and_2_out, not_2_out, not_4_out, QB);
  and and_3 (and_3_out, not_5_out, not_4_out, A);
  or or_1 (or_1_out, and_1_out, and_3_out, and_2_out, and_4_out);
  and and_4 (and_4_out, not_2_out, not_1_out, QA);
  D_Flip_Flop d_ff_1 (.clk(not_3_out), .D(or_1_out), .Q(QA), .reset(CLR));  // open: Qn, preset, en
  and and_5 (and_5_out, QA, not_1_out, not_5_out);
  and and_6 (and_6_out, not_5_out, not_4_out, B);
  or or_2 (or_2_out, and_5_out, and_6_out, and_8_out, and_7_out);
  and and_7 (and_7_out, not_2_out, not_1_out, QB);
  and and_8 (and_8_out, not_2_out, not_4_out, QC);
  and and_9 (and_9_out, QB, not_1_out, not_5_out);
  D_Flip_Flop d_ff_2 (.clk(not_3_out), .D(or_2_out), .Q(QB), .reset(CLR));  // open: Qn, preset, en
  and and_10 (and_10_out, not_5_out, not_4_out, C);
  and and_11 (and_11_out, not_2_out, not_4_out, QD);
  or or_3 (or_3_out, and_9_out, and_10_out, and_11_out, and_12_out);
  and and_12 (and_12_out, not_2_out, not_1_out, QC);
  D_Flip_Flop d_ff_3 (.clk(not_3_out), .D(or_3_out), .Q(QC), .reset(CLR));  // open: Qn, preset, en
  and and_13 (and_13_out, QC, not_1_out, not_5_out);
  and and_14 (and_14_out, not_5_out, not_4_out, D);
  and and_15 (and_15_out, not_2_out, not_4_out, SL);
  or or_4 (or_4_out, and_13_out, and_14_out, and_15_out, and_16_out);
  D_Flip_Flop d_ff_4 (.clk(not_3_out), .D(or_4_out), .Q(QD), .reset(CLR));  // open: Qn, preset, en
  and and_16 (and_16_out, not_2_out, not_1_out, QD);

  // Notes on the sheet:
  //   S0
  //   S1
  //   SR
  //   CLK
  //   RS
  //   A
  //   QA
  //   B
  //   QB
  //   C
  //   QC
  //   D
  //   SL
  //   QD
endmodule

module a (
  input  D_S1__CLR,
  input  RESET,
  input  SR,
  output QD,
  output QC,
  output QB,
  output QA
);

  wire CLK_out, not_1_out;

  Clock CLK (.out(CLK_out));
  not not_1 (not_1_out, D_S1__CLR);
  _74194 u_74194_1 (
    .S0(RESET), .S1(D_S1__CLR), .SR(SR), .CLK(CLK_out), .CLR(not_1_out), .A(1'b0), .B(1'b0), .C(1'b0),
    .D(D_S1__CLR), .SL(QA), .QA(QA), .QB(QB), .QC(QC), .QD(QD));
endmodule

module b (
  input  D,
  input  B,
  input  SR,
  input  A,
  input  C,
  input  S1__CLR,
  output QD,
  output QC,
  output QB,
  output QA
);

  wire CLK_out, nand_1_out, not_1_out;

  Clock CLK (.out(CLK_out));
  _74194 u_74194_1 (
    .S0(1'b0), .S1(S1__CLR), .SR(SR), .CLK(CLK_out), .CLR(not_1_out), .A(A), .B(B), .C(C), .D(D),
    .SL(nand_1_out), .QA(QA), .QB(QB), .QC(QC), .QD(QD));
  not not_1 (not_1_out, S1__CLR);
  nand nand_1 (nand_1_out, QD, QC, QB);
endmodule

module c (
  input  RESET,
  output QA,
  output QB,
  output QC,
  output QD
);

  wire CLK_out, not_1_out;

  Clock CLK (.out(CLK_out));
  _74194 u_74194_1 (
    .S0(1'b0), .S1(RESET), .CLK(CLK_out), .SL(not_1_out), .QA(QA), .QB(QB), .QC(QC), .QD(QD));  // open: SR, CLR, A, B, C, D
  not not_1 (not_1_out, QA);
endmodule
