// Logisim project Cwiczenia1b.circ as structural Verilog: 2 circuits, main circuit main
module main (
  input  RS,
  input  D,
  input  C,
  input  B,
  input  LS,
  input  A,
  input  in_7,
  input  [1:0] S1_S2,
  output out_9,
  output out_10,
  output out_11,
  output out_12
);

  wire clock_1_out, multiplexer_1_out, multiplexer_2_out, multiplexer_3_out, multiplexer_4_out;

  Multiplexer #(.select(2)) multiplexer_1 (
    .in0(out_9), .in1(RS), .in2(out_10), .in3(D), .out(multiplexer_1_out), .sel(S1_S2));  // open: en
  Multiplexer #(.select(2)) multiplexer_2 (
    .in0(out_10), .in1(out_9), .in2(out_11), .in3(C), .out(multiplexer_2_out), .sel(S1_S2));  // open: en
  Multiplexer #(.select(2)) multiplexer_3 (
    .in0(out_11), .in1(out_10), .in2(out_12), .in3(B), .out(multiplexer_3_out), .sel(S1_S2));  // open: en
  Multiplexer #(.select(2)) multiplexer_4 (
    .in0(out_12), .in1(out_11), .in2(LS), .in3(A), .out(multiplexer_4_out), .sel(S1_S2));  // open: en
  Clock clock_1 (.out(clock_1_out));
  D_Flip_Flop d_ff_1 (.clk(clock_1_out), .D(multiplexer_1_out), .Q(out_9), .reset(in_7));  // open: Qn, preset, en
  D_Flip_Flop d_ff_2 (.clk(clock_1_out), .D(multiplexer_2_out), .Q(out_10), .reset(in_7));  // open: Qn, preset, en
  D_Flip_Flop d_ff_3 (.clk(clock_1_out), .D(multiplexer_3_out), .Q(out_11), .reset(in_7));  // open: Qn, preset, en
  D_Flip_Flop d_ff_4 (.clk(clock_1_out), .D(multiplexer_4_out), .Q(out_12), .reset(in_7));  // open: Qn, preset, en
endmodule

module a (
  input  RS,
  input  D,
  input  C,
  input  B,
  input  LS,
  input  A,
  input  in_7,
  input  [1:0] S1_S2,
  output QD,
  output QC,
  output QB,
  output QA
);

  wire clock_1_out, multiplexer_1_out, multiplexer_2_out, multiplexer_3_out, multiplexer_4_out;

  Multiplexer #(.select(2)) multiplexer_1 (
    .in0(QD), .in1(RS), .in2(QC), .in3(D), .out(multiplexer_1_out), .sel(S1_S2));  // open: en
  Multiplexer #(.select(2)) multiplexer_2 (
    .in0(QC), .in1(QD), .in2(QB), .in3(C), .out(multiplexer_2_out), .sel(S1_S2));  // open: en
  Multiplexer #(.select(2)) multiplexer_3 (
    .in0(QB), .in1(QC), .in2(QA), .in3(B), .out(multiplexer_3_out), .sel(S1_S2));  // open: en
  Multiplexer #(.select(2)) multiplexer_4 (
    .in0(QA), .in1(QB), .in2(LS), .in3(A), .out(multiplexer_4_out), .sel(S1_S2));  // open: en
  Clock clock_1 (.out(clock_1_out));
  D_Flip_Flop d_ff_1 (.clk(clock_1_out), .D(multiplexer_1_out), .Q(QD), .reset(in_7));  // open: Qn, preset, en
  D_Flip_Flop d_ff_2 (.clk(clock_1_out), .D(multiplexer_2_out), .Q(QC), .reset(in_7));  // open: Qn, preset, en
  D_Flip_Flop d_ff_3 (.clk(clock_1_out), .D(multiplexer_3_out), .Q(QB), .reset(in_7));  // open: Qn, preset, en
  D_Flip_Flop d_ff_4 (.clk(clock_1_out), .D(multiplexer_4_out), .Q(QA), .reset(in_7));  // open: Qn, preset, en
endmodule
