// Logisim project 1.circ as structural Verilog: 10 circuits, main circuit main
module main (
  input  A,
  input  B,
  input  C,
  input  D
);
endmodule

module _1 (
  output out_1
);

  wire A_q, A_qn, B_q, B_qn, C_q, C_qn, clock_1_out, D_q, D_qn, n74151_1_o2, nor_1_out, nor_2_out, nor_3_out,
       not_1_out;

  Clock clock_1 (.out(clock_1_out));
  D_Flip_Flop A (.clk(clock_1_out), .D(A_qn), .Q(A_q), .Qn(A_qn));  // open: preset, en, reset
  D_Flip_Flop B (.clk(A_q), .D(B_qn), .Q(B_q), .Qn(B_qn));  // open: preset, en, reset
  D_Flip_Flop C (.clk(B_q), .D(C_qn), .Q(C_q), .Qn(C_qn));  // open: preset, en, reset
  D_Flip_Flop D (.clk(C_q), .D(D_qn), .Q(D_q), .Qn(D_qn));  // open: preset, en, reset
  _74151 u_74151_1 (
    .G(D_q), .D0(1'b1), .D1(1'b1), .D2(1'b1), .D3(1'b1), .D4(1'b1), .D5(1'b0), .D6(1'b0), .D7(1'b0), .A(A_q),
    .B(B_q), .C(C_q), .O2(n74151_1_o2));  // open: O1
  nor nor_1 (nor_1_out, A_q, B_q);
  not not_1 (not_1_out, C_q);
  nor nor_2 (nor_2_out, nor_1_out, not_1_out);
  nor nor_3 (nor_3_out, nor_2_out, D_q);
  xnor xnor_1 (out_1, nor_3_out, n74151_1_o2);

  // Notes on the sheet:
  //   Układ a)
endmodule

module NAND_ONLY (
  input  A,
  input  B,
  input  C,
  input  D,
  output Q
);

  wire nand_1_out, nand_2_out, nand_3_out, nand_4_out, nand_5_out, nand_6_out;

  nand nand_1 (nand_1_out, A, A);
  nand nand_2 (nand_2_out, B, B);
  nand nand_3 (nand_3_out, nand_1_out, nand_2_out);
  nand nand_4 (nand_4_out, nand_3_out, C);
  nand nand_5 (nand_5_out, D, D);
  nand nand_6 (nand_6_out, nand_4_out, nand_5_out);
  nand nand_7 (Q, nand_6_out, nand_6_out);
endmodule

module _2 (
  input  A,
  input  B,
  input  C,
  input  A_2,
  input  B_2,
  input  C_2,
  output out_7,
  output out_8,
  output out_9
);

  wire A_q, A_qn, and_1_out, and_2_out, and_3_out, and_4_out, and_5_out, and_6_out, B_q, B_qn, C_q, C_qn,
       clock_1_out, n74151_1_o2, nand_1_out, nand_2_out, nand_3_out, nand_4_out, nand_5_out, nand_6_out,
       nand_7_out, nand_8_out, nand_9_out, nand_10_out, nand_11_out, nand_12_out, nand_13_out, not_1_out,
       not_2_out, not_3_out, not_4_out, not_5_out, not_6_out, or_2_out;

  Clock clock_1 (.out(clock_1_out));
  D_Flip_Flop u_A (.clk(clock_1_out), .D(A_qn), .Q(A_q), .Qn(A_qn));  // open: preset, en, reset
  not not_1 (not_1_out, C_2);
  not not_2 (not_2_out, B_2);
  not not_3 (not_3_out, A_2);
  D_Flip_Flop u_B (.clk(A_q), .D(B_qn), .Q(B_q), .Qn(B_qn));  // open: preset, en, reset
  and and_1 (and_1_out, A_2, B_2);
  and and_2 (and_2_out, not_2_out, not_3_out);
  and and_3 (and_3_out, and_1_out, not_1_out);
  and and_4 (and_4_out, and_2_out, C_2);
  D_Flip_Flop u_C (.clk(B_q), .D(C_qn), .Q(C_q), .Qn(C_qn));  // open: preset, en, reset
  or or_1 (out_8, and_3_out, and_4_out);
  and and_5 (and_5_out, A_q, B_q, not_4_out);
  not not_4 (not_4_out, C_q);
  not not_5 (not_5_out, A_q);
  and and_6 (and_6_out, not_5_out, not_6_out, C_q);
  not not_6 (not_6_out, B_q);
  _74151 u_74151_1 (
    .G(1'b0), .D0(1'b0), .D1(1'b0), .D2(1'b0), .D3(1'b1), .D4(1'b1), .D5(1'b0), .D6(1'b0), .D7(1'b0),
    .A(A_q), .B(B_q), .C(C_q), .O2(n74151_1_o2));  // open: O1
  nand nand_1 (nand_1_out, A, B);
  nand nand_2 (nand_2_out, C, C);
  nand nand_3 (nand_3_out, A, A);
  nand nand_4 (nand_4_out, B, B);
  or or_2 (or_2_out, and_5_out, and_6_out);
  nand nand_5 (nand_5_out, nand_1_out, nand_1_out);
  nand nand_6 (nand_6_out, nand_5_out, nand_2_out);
  nand nand_7 (nand_7_out, nand_3_out, nand_4_out);
  xnor xnor_1 (out_9, or_2_out, n74151_1_o2);
  nand nand_8 (nand_8_out, nand_6_out, nand_6_out);
  nand nand_9 (nand_9_out, nand_7_out, nand_7_out);
  nand nand_10 (nand_10_out, nand_9_out, C);
  nand nand_11 (nand_11_out, nand_10_out, nand_10_out);
  nand nand_12 (nand_12_out, nand_8_out, nand_8_out);
  nand nand_13 (nand_13_out, nand_11_out, nand_11_out);
  nand nand_14 (out_7, nand_12_out, nand_13_out);

  // Notes on the sheet:
  //   b)
endmodule

module _74151 (
  input  G,
  input  D0,
  input  D1,
  input  D2,
  input  D3,
  input  D4,
  input  D5,
  input  D6,
  input  D7,
  input  A,
  input  B,
  input  C,
  output O2,
  output O1
);

  wire and_1_out, and_2_out, and_3_out, and_4_out, and_5_out, and_6_out, and_7_out, and_8_out, not_1_out,
       not_2_out, not_3_out, not_4_out;

  not not_1 (not_1_out, G);
  not not_2 (not_2_out, A);
  not not_3 (not_3_out, B);
  not not_4 (not_4_out, C);
  and and_1 (and_1_out, not_1_out, D0, not_2_out, not_3_out, not_4_out);
  and and_2 (and_2_out, not_1_out, D1, A, not_3_out, not_4_out);
  and and_3 (and_3_out, not_1_out, D2, not_2_out, B, not_4_out);
  and and_4 (and_4_out, not_1_out, D3, A, B, not_4_out);
  and and_5 (and_5_out, not_1_out, D4, not_2_out, not_3_out, C);
  and and_6 (and_6_out, not_1_out, D5, A, not_3_out, C);
  and and_7 (and_7_out, not_1_out, D6, not_2_out, B, C);
  and and_8 (and_8_out, not_1_out, D7, A, B, C);
  nor nor_1 (O1, and_1_out, and_2_out, and_3_out, and_4_out, and_5_out, and_6_out, and_7_out, and_8_out);
  not not_5 (O2, O1);
endmodule

module _2_nand_only (
  input  A,
  input  B,
  input  C,
  output out_4
);

  wire nand_1_out, nand_2_out, nand_3_out, nand_4_out, nand_5_out, nand_6_out, nand_7_out, nand_8_out,
       nand_9_out, nand_10_out, nand_11_out, nand_12_out, nand_13_out;

  nand nand_1 (nand_1_out, A, B);
  nand nand_2 (nand_2_out, nand_1_out, nand_1_out);
  nand nand_3 (nand_3_out, C, C);
  nand nand_4 (nand_4_out, A, A);
  nand nand_5 (nand_5_out, B, B);
  nand nand_6 (nand_6_out, nand_4_out, nand_5_out);
  nand nand_7 (nand_7_out, nand_2_out, nand_3_out);
  nand nand_8 (nand_8_out, nand_6_out, nand_6_out);
  nand nand_9 (nand_9_out, nand_7_out, nand_7_out);
  nand nand_10 (nand_10_out, nand_8_out, C);
  nand nand_11 (nand_11_out, nand_10_out, nand_10_out);
  nand nand_12 (nand_12_out, nand_9_out, nand_9_out);
  nand nand_13 (nand_13_out, nand_11_out, nand_11_out);
  nand nand_14 (out_4, nand_12_out, nand_13_out);
endmodule

module a_mux (
  input  D,
  input  A,
  input  B,
  input  C,
  output out_5
);

  _74151 u_74151_1 (
    .G(D), .D0(1'b1), .D1(1'b1), .D2(1'b1), .D3(1'b1), .D4(1'b1), .D5(1'b0), .D6(1'b0), .D7(1'b0), .A(A),
    .B(B), .C(C), .O2(out_5));  // open: O1
endmodule

module b_mux (
  input  A,
  input  B,
  input  C,
  output out_4
);

  _74151 u_74151_1 (
    .G(1'b0), .D0(1'b0), .D1(1'b0), .D2(1'b0), .D3(1'b1), .D4(1'b1), .D5(1'b0), .D6(1'b0), .D7(1'b0), .A(A),
    .B(B), .C(C), .O2(out_4));  // open: O1
endmodule

module a (
  input  in_1,
  input  in_2,
  input  in_3,
  input  in_4
);

  wire and_1_out, and_2_out, or_1_out;

  and and_1 (and_1_out, ~in_1, ~in_2, ~in_4);  // AND_Gate
  and and_2 (and_2_out, ~in_3, ~in_4);  // AND_Gate
  or or_1 (or_1_out, and_1_out, and_2_out);
endmodule

module b (
  input  in_1,
  input  in_2,
  input  in_3
);

  wire and_1_out, and_2_out, or_1_out;

  and and_1 (and_1_out, in_1, in_2, ~in_3);  // AND_Gate
  and and_2 (and_2_out, ~in_1, ~in_2, in_3);  // AND_Gate
  or or_1 (or_1_out, and_1_out, and_2_out);
endmodule
