// Logisim project Zadanie2.circ as structural Verilog: 5 circuits, main circuit uklad2NAND
module uklad2NAND (
  input  A,
  input  B,
  input  C,
  output out_4
);

  wire nand_1_out, nand_2_out, nand_3_out, nand_4_out, nand_5_out;

  nand nand_1 (nand_1_out, A, A);
  nand nand_2 (nand_2_out, B, B);
  nand nand_3 (nand_3_out, C, C);
  nand nand_4 (nand_4_out, A, B, nand_3_out);
  nand nand_5 (nand_5_out, nand_1_out, nand_2_out, C);
  nand nand_6 (out_4, nand_4_out, nand_5_out);
endmodule

module uklad1NAND (
  input  A,
  input  B,
  input  C,
  input  in_4,
  output out_5
);

  wire nand_1_out, nand_2_out, nand_3_out, nand_4_out, nand_5_out, nand_6_out;

  nand nand_1 (nand_1_out, A, A);
  nand nand_2 (nand_2_out, B, B);
  nand nand_3 (nand_3_out, C, C);
  nand nand_4 (nand_4_out, in_4, in_4);
  nand nand_5 (nand_5_out, nand_1_out, nand_2_out, nand_4_out);
  nand nand_6 (nand_6_out, nand_3_out, nand_4_out);
  nand nand_7 (out_5, nand_5_out, nand_6_out);
endmodule

module _7151 (
  input  G,
  input  D0,
  input  D1,
  input  D2,
  input  D3,
  input  D4,
  input  D5,
  input  D6,
  input  D7,
  input  A,
  input  B,
  input  C,
  output out_13,
  output out_14
);

  wire and_1_out, and_2_out, and_3_out, and_4_out, and_5_out, and_6_out, and_7_out, and_8_out, not_1_out,
       not_2_out, not_3_out, not_4_out, not_5_out, not_6_out, not_7_out;

  not not_1 (not_1_out, A);
  not not_2 (not_2_out, B);
  not not_3 (not_3_out, C);
  not not_4 (not_4_out, G);
  not not_5 (not_5_out, not_1_out);
  not not_6 (not_6_out, not_2_out);
  not not_7 (not_7_out, not_3_out);
  and and_1 (and_1_out, not_2_out, not_1_out, not_3_out, D0, not_4_out);
  and and_2 (and_2_out, not_2_out, not_5_out, not_3_out, D1, not_4_out);
  and and_3 (and_3_out, not_6_out, not_1_out, not_3_out, D2, not_4_out);
  and and_4 (and_4_out, not_6_out, not_5_out, not_3_out, D3, not_4_out);
  and and_5 (and_5_out, not_7_out, not_2_out, not_1_out, D4, not_4_out);
  and and_6 (and_6_out, not_2_out, not_5_out, not_7_out, D5, not_4_out);
  and and_7 (and_7_out, not_6_out, not_1_out, not_7_out, D6, not_4_out);
  and and_8 (and_8_out, not_6_out, not_5_out, not_7_out, D7, not_4_out);
  nor nor_1 (out_14, and_1_out, and_2_out, and_3_out, and_4_out, and_5_out, and_6_out, and_7_out, and_8_out);
  not not_8 (out_13, out_14);
endmodule

module uklad1MUX (
  input  D,
  input  A,
  input  B,
  input  C,
  output out_5
);

  _7151 u_7151_1 (
    .G(D), .D0(1'b1), .D1(1'b1), .D2(1'b1), .D3(1'b1), .D4(1'b1), .D5(1'b0), .D6(1'b0), .D7(1'b0), .A(A),
    .B(B), .C(C), .out_13(out_5));  // open: out_14
endmodule

module uklad2MUX (
  input  A,
  input  B,
  input  C,
  output out_4
);

  _7151 u_7151_1 (
    .G(1'b0), .D0(1'b0), .D1(1'b0), .D2(1'b0), .D3(1'b1), .D4(1'b1), .D5(1'b0), .D6(1'b0), .D7(1'b0), .A(A),
    .B(B), .C(C), .out_13(out_4));  // open: out_14
endmodule
