// Logisim project Zadanie3.circ as structural Verilog
module a (
  input  A,
  input  B,
  input  C,
  input  D
);

  wire n7474_1__5__q1, n7474_1__6__nq1, nand_1_out, nand_2_out, nand_3_out, nand_4_out, nand_5_out,
       nand_6_out, nand_7_out, nand_8_out, nand_9_out;

  nand nand_1 (nand_1_out, A, A);
  nand nand_2 (nand_2_out, nand_1_out, B);
  nand nand_3 (nand_3_out, C, C);
  nand nand_4 (nand_4_out, C, D);
  nand nand_5 (nand_5_out, nand_2_out, nand_2_out);
  nand nand_6 (nand_6_out, nand_4_out, nand_4_out);
  nand nand_7 (nand_7_out, nand_5_out, nand_3_out);
  nand nand_8 (nand_8_out, nand_6_out, nand_6_out);
  nand nand_9 (nand_9_out, nand_7_out, nand_8_out);
  LED LED1 (.in(nand_9_out));
  LED LED2 (.in(n7474_1__5__q1));
  _7474 u_7474_1 (
    ._1__CLR1(1'b0), ._2__D1(n7474_1__6__nq1), ._3__CLK1(nand_9_out), ._4__PR1(1'b0),
    ._5__Q1(n7474_1__5__q1), ._6__nQ1(n7474_1__6__nq1), ._7__GND(1'b0), ._14__Vcc(1'b1));  // open: _13__CLR2, _12__D2, _11__CLK2, _10__PR2, _9__Q2, _8__nQ2
endmodule

module _7474 (
  input  _1__CLR1,
  input  _14__Vcc,
  input  _2__D1,
  input  _13__CLR2,
  input  _3__CLK1,
  input  _12__D2,
  input  _4__PR1,
  input  _11__CLK2,
  input  _10__PR2,
  input  _7__GND,
  output _5__Q1,
  output _6__nQ1,
  output _9__Q2,
  output _8__nQ2
);

  D_Flip_Flop d_ff_1 (
    .clk(_3__CLK1), .D(_2__D1), .Q(_5__Q1), .Qn(_6__nQ1), .preset(_4__PR1), .reset(_1__CLR1));  // open: en
  D_Flip_Flop d_ff_2 (
    .clk(_11__CLK2), .D(_12__D2), .Q(_9__Q2), .Qn(_8__nQ2), .preset(_10__PR2), .reset(_13__CLR2));  // open: en

  // Notes on the sheet:
  //   7474: dual D-type flip flop
endmodule

module a_gen (
  input  A,
  input  B,
  input  C,
  input  D,
  input  A_2,
  input  B_2,
  input  C_2,
  input  D_2
);

  wire d_ff_1_q, d_ff_1_qn, n7474_1__5__q1, n7474_1__6__nq1, nand_1_out, nand_2_out, nand_3_out, nand_4_out,
       nand_5_out, nand_6_out, nand_7_out, nand_8_out, nand_9_out, nand_10_out, nand_11_out, nand_12_out,
       nand_13_out, nand_14_out;

  nand nand_1 (nand_1_out, A, A);
  nand nand_2 (nand_2_out, A_2, A_2);
  nand nand_3 (nand_3_out, nand_1_out, B);
  nand nand_4 (nand_4_out, nand_2_out, B_2);
  nand nand_5 (nand_5_out, nand_3_out, nand_3_out);
  nand nand_6 (nand_6_out, C, C);
  nand nand_7 (nand_7_out, nand_4_out, nand_4_out);
  nand nand_8 (nand_8_out, C_2, C_2);
  nand nand_9 (nand_9_out, nand_5_out, nand_6_out);
  nand nand_10 (nand_10_out, C, D);
  nand nand_11 (nand_11_out, nand_7_out, nand_8_out);
  nand nand_12 (nand_12_out, C_2, D_2);
  nand nand_13 (nand_13_out, nand_9_out, nand_10_out);
  LED LED1 (.in(nand_13_out));
  nand nand_14 (nand_14_out, nand_11_out, nand_12_out);
  _7474 u_7474_1 (
    ._1__CLR1(1'b0), ._2__D1(n7474_1__6__nq1), ._3__CLK1(nand_13_out), ._4__PR1(1'b0),
    ._5__Q1(n7474_1__5__q1), ._6__nQ1(n7474_1__6__nq1), ._7__GND(1'b0), ._14__Vcc(1'b1));  // open: _13__CLR2, _12__D2, _11__CLK2, _10__PR2, _9__Q2, _8__nQ2
  LED LED2 (.in(n7474_1__5__q1));
  LED LED1_2 (.in(nand_14_out));
  D_Flip_Flop d_ff_1 (.clk(nand_14_out), .D(d_ff_1_qn), .Q(d_ff_1_q), .Qn(d_ff_1_qn));  // open: preset, en, reset
  LED LED2_2 (.in(d_ff_1_q));
endmodule

module a_bezHazardu (
  input  A,
  input  B,
  input  C,
  input  D
);

  wire n7474_1__5__q1, n7474_1__6__nq1, nand_1_out, nand_2_out, nand_3_out, nand_4_out, nand_5_out,
       nand_6_out, nand_7_out, nand_8_out, nand_9_out, nand_10_out, nand_11_out, nand_12_out, nand_13_out,
       nand_14_out, nand_15_out, nand_16_out;

  nand nand_1 (nand_1_out, A, A);
  nand nand_2 (nand_2_out, nand_1_out, B);
  nand nand_3 (nand_3_out, C, C);
  nand nand_4 (nand_4_out, C, D);
  nand nand_5 (nand_5_out, nand_1_out, B);
  nand nand_6 (nand_6_out, nand_4_out, nand_4_out);
  nand nand_7 (nand_7_out, nand_5_out, nand_5_out);
  nand nand_8 (nand_8_out, nand_2_out, nand_2_out);
  nand nand_9 (nand_9_out, nand_7_out, D);
  nand nand_10 (nand_10_out, nand_8_out, nand_3_out);
  nand nand_11 (nand_11_out, nand_6_out, nand_6_out);
  nand nand_12 (nand_12_out, nand_9_out, nand_9_out);
  nand nand_13 (nand_13_out, nand_10_out, nand_11_out);
  nand nand_14 (nand_14_out, nand_13_out, nand_13_out);
  nand nand_15 (nand_15_out, nand_12_out, nand_12_out);
  nand nand_16 (nand_16_out, nand_14_out, nand_15_out);
  LED LED1 (.in(nand_16_out));
  LED LED2 (.in(n7474_1__5__q1));
  _7474 u_7474_1 (
    ._1__CLR1(1'b0), ._2__D1(n7474_1__6__nq1), ._3__CLK1(nand_16_out), ._4__PR1(1'b0),
    ._5__Q1(n7474_1__5__q1), ._6__nQ1(n7474_1__6__nq1), ._7__GND(1'b0), ._14__Vcc(1'b1));  // open: _13__CLR2, _12__D2, _11__CLK2, _10__PR2, _9__Q2, _8__nQ2
endmodule
