// Logisim project zadanie3a.circ as structural Verilog: 3 circuits, main circuit funkcjazhazardem
module funkcjazhazardem (
  input  A,
  input  B,
  input  C,
  input  D,
  output out_5
);

  wire nand_1_out, nand_2_out, nand_3_out, not_1_out, not_2_out, not_3_out;

  not not_1 (not_1_out, A);
  not not_2 (not_2_out, C);
  not not_3 (not_3_out, D);
  nand nand_1 (nand_1_out, A, B);
  nand nand_2 (nand_2_out, not_1_out, C, D);
  nand nand_3 (nand_3_out, A, not_2_out, not_3_out);
  nand nand_4 (out_5, nand_1_out, nand_2_out, nand_3_out);
endmodule

module funkcjabezhazardu (
  input  A,
  input  B,
  input  C,
  input  D,
  output out_5
);

  wire nand_1_out, nand_2_out, nand_3_out, nand_4_out, not_1_out, not_2_out, not_3_out;

  not not_1 (not_1_out, A);
  not not_2 (not_2_out, C);
  not not_3 (not_3_out, D);
  nand nand_1 (nand_1_out, A, B);
  nand nand_2 (nand_2_out, not_1_out, C, D);
  nand nand_3 (nand_3_out, A, not_2_out, not_3_out);
  nand nand_4 (nand_4_out, B, D, C);
  nand nand_5 (out_5, nand_1_out, nand_2_out, nand_3_out, nand_4_out);
endmodule

module OSCYLOSKOP (
  input  A,
  input  B,
  input  C,
  input  D
);

  wire d_ff_1_q, d_ff_1_qn, d_ff_2_q, d_ff_2_qn, nand_1_out, nand_2_out, nand_3_out, nand_4_out, nand_5_out,
       nand_6_out, nand_7_out, nand_8_out, nand_9_out, not_1_out, not_2_out, not_3_out, not_4_out, not_5_out,
       not_6_out;

  not not_1 (not_1_out, A);
  not not_2 (not_2_out, A);
  not not_3 (not_3_out, C);
  not not_4 (not_4_out, D);
  not not_5 (not_5_out, C);
  not not_6 (not_6_out, D);
  nand nand_1 (nand_1_out, A, B);
  nand nand_2 (nand_2_out, not_2_out, C, D);
  nand nand_3 (nand_3_out, A, not_3_out, not_4_out);
  nand nand_4 (nand_4_out, A, B);
  nand nand_5 (nand_5_out, not_1_out, C, D);
  nand nand_6 (nand_6_out, A, not_5_out, not_6_out);
  nand nand_7 (nand_7_out, B, D, C);
  nand nand_8 (nand_8_out, nand_1_out, nand_2_out, nand_3_out);
  nand nand_9 (nand_9_out, nand_4_out, nand_5_out, nand_6_out, nand_7_out);
  LED led_1 (.in(nand_8_out));
  LED led_2 (.in(nand_9_out));
  D_Flip_Flop d_ff_1 (.clk(nand_8_out), .D(d_ff_1_qn), .Q(d_ff_1_q), .Qn(d_ff_1_qn));  // open: preset, en, reset
  D_Flip_Flop d_ff_2 (.clk(nand_9_out), .D(d_ff_2_qn), .Q(d_ff_2_q), .Qn(d_ff_2_qn));  // open: preset, en, reset
  LED led_3 (.in(d_ff_1_q));
  LED led_4 (.in(d_ff_2_q));
endmodule
