// Logisim project Zadanie4.circ as structural Verilog: 2 circuits, main circuit main
module main (
  input  in_1,
  output out_2
);

  wire and_1_out, and_2_out, and_3_out, clock_1_out, d_ff_1_q, d_ff_1_qn, d_ff_2_q, or_1_out, or_2_out;

  Clock clock_1 (.out(clock_1_out));
  and and_1 (and_1_out, d_ff_1_qn, in_1);
  and and_2 (and_2_out, in_1, d_ff_2_q);
  and and_3 (and_3_out, in_1, d_ff_1_q);
  or or_1 (or_1_out, and_1_out, and_2_out);
  or or_2 (or_2_out, and_2_out, and_3_out);
  D_Flip_Flop #(.trigger("high")) d_ff_1 (
    .clk(clock_1_out), .D(or_1_out), .Q(d_ff_1_q), .Qn(d_ff_1_qn));  // open: preset, en, reset
  D_Flip_Flop #(.trigger("high")) d_ff_2 (
    .clk(clock_1_out), .D(or_2_out), .Q(d_ff_2_q));  // open: Qn, preset, en, reset
  and and_4 (out_2, d_ff_1_q, d_ff_2_q);
endmodule

module SameCircuitUsingNAND (
  input  in_1,
  output out_2
);

  wire clock_1_out, nand_1_out, nand_2_out, nand_3_out, nand_4_out, nand_5_out, nand_6_out, nand_7_out,
       nand_8_out, nand_9_out, nand_10_out, nand_11_out, nand_12_out, nand_13_out, nand_14_out, nand_15_out,
       nand_16_out, nand_17_out, nand_18_out, nand_19_out, nand_20_out, nand_21_out, nand_22_out, nand_23_out;

  nand nand_1 (nand_1_out, nand_21_out, in_1);
  nand nand_2 (nand_2_out, in_1, nand_19_out);
  nand nand_3 (nand_3_out, in_1, nand_17_out);
  nand nand_4 (nand_4_out, nand_1_out, nand_1_out);
  nand nand_5 (nand_5_out, nand_2_out, nand_2_out);
  nand nand_6 (nand_6_out, nand_3_out, nand_3_out);
  nand nand_7 (nand_7_out, nand_4_out, nand_4_out);
  nand nand_8 (nand_8_out, nand_5_out, nand_5_out);
  nand nand_9 (nand_9_out, nand_5_out, nand_5_out);
  nand nand_10 (nand_10_out, nand_6_out, nand_6_out);
  nand nand_11 (nand_11_out, nand_7_out, nand_8_out);
  nand nand_12 (nand_12_out, nand_9_out, nand_10_out);
  Clock clock_1 (.out(clock_1_out));
  nand nand_13 (nand_13_out, nand_11_out, clock_1_out);
  nand nand_14 (nand_14_out, nand_11_out, nand_11_out);
  nand nand_15 (nand_15_out, nand_12_out, clock_1_out);
  nand nand_16 (nand_16_out, nand_12_out, nand_12_out);
  nand nand_17 (nand_17_out, nand_13_out, nand_21_out);
  nand nand_18 (nand_18_out, clock_1_out, nand_14_out);
  nand nand_19 (nand_19_out, nand_15_out, nand_22_out);
  nand nand_20 (nand_20_out, clock_1_out, nand_16_out);
  nand nand_21 (nand_21_out, nand_17_out, nand_18_out);
  nand nand_22 (nand_22_out, nand_19_out, nand_20_out);
  nand nand_23 (nand_23_out, nand_17_out, nand_19_out);
  nand nand_24 (out_2, nand_23_out, nand_23_out);

  // Notes on the sheet:
  //   Układ ten działa tylko na High, nie na Rising edge, oraz dalej używamy NANDU jako NOT, co jest niezgodne z poleceniem
endmodule
