// Logisim project zadanie4 (2).circ as structural Verilog: 5 circuits, main circuit układnormalny
module \układnormalny  (
  input  X,
  output Z
);

  wire and_1_out, and_2_out, and_3_out, clock_1_out, d_ff_1_q, d_ff_1_qn, d_ff_2_q, or_1_out, or_2_out;

  and and_1 (and_1_out, d_ff_1_qn, X);
  and and_2 (and_2_out, X, d_ff_2_q);
  and and_3 (and_3_out, X, d_ff_1_q);
  or or_1 (or_1_out, and_1_out, and_2_out);
  or or_2 (or_2_out, and_2_out, and_3_out);
  Clock clock_1 (.out(clock_1_out));
  D_Flip_Flop d_ff_1 (.clk(clock_1_out), .D(or_1_out), .Q(d_ff_1_q), .Qn(d_ff_1_qn));  // open: preset, en, reset
  D_Flip_Flop d_ff_2 (.clk(clock_1_out), .D(or_2_out), .Q(d_ff_2_q));  // open: Qn, preset, en, reset
  and and_4 (Z, d_ff_1_q, d_ff_2_q);
endmodule

module ukladNAND (
  input  X,
  output Z
);

  wire clock_1_out, d_ff_1_q, d_ff_1_qn, d_ff_2_q, nand_1_out, nand_2_out, nand_3_out, nand_4_out,
       nand_5_out, nand_6_out;

  nand nand_1 (nand_1_out, X, d_ff_2_q);
  nand nand_2 (nand_2_out, d_ff_1_qn, X);
  nand nand_3 (nand_3_out, X, d_ff_1_q);
  nand nand_4 (nand_4_out, nand_2_out, nand_1_out);
  nand nand_5 (nand_5_out, nand_1_out, nand_3_out);
  Clock clock_1 (.out(clock_1_out));
  D_Flip_Flop d_ff_1 (.clk(clock_1_out), .D(nand_4_out), .Q(d_ff_1_q), .Qn(d_ff_1_qn));  // open: preset, en, reset
  D_Flip_Flop d_ff_2 (.clk(clock_1_out), .D(nand_5_out), .Q(d_ff_2_q));  // open: Qn, preset, en, reset
  nand nand_6 (nand_6_out, d_ff_1_q, d_ff_2_q);
  not nor_1 (Z, nand_6_out);  // NOR_Gate
endmodule

module przerzutnikD (
  input  in_1,
  input  in_2,
  output out_3,
  output out_4
);

  wire nand_1_out, nand_2_out;

  nand nand_1 (nand_1_out, in_1, in_2);
  nand nand_2 (nand_2_out, nand_1_out, in_2);
  nand nand_3 (out_3, nand_1_out, out_4);
  nand nand_4 (out_4, out_3, nand_2_out);
endmodule

module uklad1 (
  input  in_1,
  input  in_2,
  input  in_3,
  input  in_4,
  input  in_5,
  output out_6,
  output out_7,
  output out_8,
  output out_9,
  output out_10
);

  wire and_1_out, and_2_out, and_3_out, clock_1_out, d_ff_1_q, d_ff_1_qn, d_ff_2_q, nand_1_out, nand_2_out,
       nand_3_out, nand_4_out, nand_5_out, nand_6_out, nand_7_out, nand_8_out, nand_9_out, nand_10_out,
       nand_11_out, nand_12_out, not_1_out, not_2_out, or_1_out, or_2_out;

  and and_1 (and_1_out, d_ff_1_qn, in_5);
  and and_2 (and_2_out, in_5, d_ff_2_q);
  and and_3 (and_3_out, in_5, d_ff_1_q);
  or or_1 (or_1_out, and_1_out, and_2_out);
  or or_2 (or_2_out, and_2_out, and_3_out);
  Clock clock_1 (.out(clock_1_out));
  D_Flip_Flop d_ff_1 (.clk(clock_1_out), .D(or_1_out), .Q(d_ff_1_q), .Qn(d_ff_1_qn));  // open: preset, en, reset
  D_Flip_Flop d_ff_2 (.clk(clock_1_out), .D(or_2_out), .Q(d_ff_2_q));  // open: Qn, preset, en, reset
  nand nand_1 (nand_1_out, in_1, in_2);
  nand nand_2 (nand_2_out, nand_1_out, in_2);
  nand nand_3 (nand_3_out, in_3, in_4);
  nand nand_4 (nand_4_out, nand_3_out, in_4);
  nand nand_5 (nand_5_out, nand_1_out, nand_6_out);
  nand nand_6 (nand_6_out, nand_5_out, nand_2_out);
  not not_1 (not_1_out, in_2);
  nand nand_7 (nand_7_out, nand_3_out, nand_8_out);
  nand nand_8 (nand_8_out, nand_7_out, nand_4_out);
  not not_2 (not_2_out, in_4);
  nand nand_9 (nand_9_out, nand_5_out, not_1_out);
  nand nand_10 (nand_10_out, nand_9_out, not_1_out);
  nand nand_11 (nand_11_out, nand_7_out, not_2_out);
  nand nand_12 (nand_12_out, nand_11_out, not_2_out);
  and and_4 (out_10, d_ff_1_q, d_ff_2_q);
  nand nand_13 (out_6, nand_9_out, out_7);
  nand nand_14 (out_7, out_6, nand_10_out);
  nand nand_15 (out_8, nand_11_out, out_9);
  nand nand_16 (out_9, out_8, nand_12_out);
endmodule

module ukladJK (
  input  in_1,
  output out_2
);

  wire and_1_out, clock_1_out, j_k_ff_1_q, j_k_ff_2_q, j_k_ff_2_qn, not_1_out;

  Clock clock_1 (.out(clock_1_out));
  not not_1 (not_1_out, in_1);
  and and_1 (and_1_out, not_1_out, clock_1_out);
  J_K_Flip_Flop #(.trigger("falling")) j_k_ff_1 (
    .J(in_1), .clk(clock_1_out), .K(j_k_ff_2_qn), .Q(j_k_ff_1_q), .reset(and_1_out));  // open: Qn, preset, en
  J_K_Flip_Flop #(.trigger("falling")) j_k_ff_2 (
    .J(j_k_ff_1_q), .clk(clock_1_out), .K(not_1_out), .Q(j_k_ff_2_q), .Qn(j_k_ff_2_qn), .reset(and_1_out));  // open: preset, en
  and and_2 (out_2, j_k_ff_1_q, j_k_ff_2_q);
endmodule
