// Logisim project zadanie5.circ as structural Verilog: 6 circuits, main circuit pierwszawersja
module pierwszawersja (
  input  in_1,
  output out_2,
  output out_3
);

  wire and_1_out, and_2_out, clock_1_out, d_ff_1_q, d_ff_1_qn;

  Clock clock_1 (.out(clock_1_out));
  D_Flip_Flop d_ff_1 (
    .clk(clock_1_out), .D(d_ff_1_qn), .Q(d_ff_1_q), .Qn(d_ff_1_qn), .en(in_1));  // open: preset, reset
  and and_1 (and_1_out, in_1, d_ff_1_q);
  and and_2 (and_2_out, d_ff_1_qn, in_1);
  Clock clock_2 ();  // open: out
  D_Flip_Flop d_ff_2 (.clk(clock_1_out), .D(and_1_out), .Q(out_2));  // open: Qn, preset, en, reset
  D_Flip_Flop d_ff_3 (.clk(clock_1_out), .D(and_2_out), .Q(out_3));  // open: Qn, preset, en, reset
endmodule

module moore__dodatkowy_przerzutnik (
  input  in_1,
  output out_2,
  output out_3
);

  wire and_1_out, and_2_out, and_3_out, clock_1_out, d_ff_1_q, d_ff_1_qn;

  Clock clock_1 (.out(clock_1_out));
  and and_1 (and_1_out, in_1, clock_1_out);
  D_Flip_Flop d_ff_1 (.clk(and_1_out), .D(d_ff_1_qn), .Q(d_ff_1_q), .Qn(d_ff_1_qn));  // open: preset, en, reset
  and and_2 (and_2_out, in_1, d_ff_1_q);
  and and_3 (and_3_out, d_ff_1_qn, in_1);
  D_Flip_Flop d_ff_2 (.clk(clock_1_out), .D(and_2_out), .Q(out_2));  // open: Qn, preset, en, reset
  D_Flip_Flop d_ff_3 (.clk(clock_1_out), .D(and_3_out), .Q(out_3));  // open: Qn, preset, en, reset
endmodule

module mealy_dodatkowy_przerzutnik (
  input  in_1,
  output out_2,
  output out_3
);

  wire and_1_out, and_2_out, and_3_out, clock_1_out, d_ff_1_q, d_ff_1_qn, d_ff_2_q, d_ff_3_q;

  Clock clock_1 (.out(clock_1_out));
  and and_1 (and_1_out, in_1, clock_1_out);
  D_Flip_Flop d_ff_1 (.clk(and_1_out), .D(d_ff_1_qn), .Q(d_ff_1_q), .Qn(d_ff_1_qn));  // open: preset, en, reset
  and and_2 (and_2_out, in_1, d_ff_1_q);
  and and_3 (and_3_out, d_ff_1_qn, in_1);
  D_Flip_Flop d_ff_2 (.clk(clock_1_out), .D(and_2_out), .Q(d_ff_2_q));  // open: Qn, preset, en, reset
  D_Flip_Flop d_ff_3 (.clk(clock_1_out), .D(and_3_out), .Q(d_ff_3_q));  // open: Qn, preset, en, reset
  and and_4 (out_2, in_1, d_ff_2_q);
  and and_5 (out_3, in_1, d_ff_3_q);
endmodule

module MooreDOBRY (
  input  in_1,
  output out_2,
  output out_3
);

  wire and_1_out, and_2_out, clock_1_out, d_ff_1_q, d_ff_1_qn, d_ff_2_q, not_1_out, or_1_out, xor_1_out;

  Clock clock_1 (.out(clock_1_out));
  not not_1 (not_1_out, in_1);
  and and_1 (and_1_out, d_ff_1_qn, in_1);
  and and_2 (and_2_out, d_ff_1_q, not_1_out);
  or or_1 (or_1_out, and_1_out, and_2_out);
  D_Flip_Flop d_ff_1 (.clk(clock_1_out), .D(or_1_out), .Q(d_ff_1_q), .Qn(d_ff_1_qn));  // open: preset, en, reset
  D_Flip_Flop d_ff_2 (.clk(clock_1_out), .D(d_ff_1_q), .Q(d_ff_2_q));  // open: Qn, preset, en, reset
  xor xor_1 (xor_1_out, d_ff_1_q, d_ff_2_q);
  and and_3 (out_2, d_ff_1_q, xor_1_out);
  and and_4 (out_3, xor_1_out, d_ff_2_q);
endmodule

module MealyDOBRY (
  input  in_1,
  output out_2,
  output out_3
);

  wire and_1_out, and_2_out, and_3_out, and_4_out, clock_1_out, d_ff_1_q, d_ff_1_qn, d_ff_2_q, not_1_out,
       or_1_out, xor_1_out;

  Clock clock_1 (.out(clock_1_out));
  not not_1 (not_1_out, in_1);
  and and_1 (and_1_out, d_ff_1_qn, in_1);
  and and_2 (and_2_out, d_ff_1_q, not_1_out);
  or or_1 (or_1_out, and_1_out, and_2_out);
  D_Flip_Flop d_ff_1 (.clk(clock_1_out), .D(or_1_out), .Q(d_ff_1_q), .Qn(d_ff_1_qn));  // open: preset, en, reset
  D_Flip_Flop d_ff_2 (.clk(clock_1_out), .D(d_ff_1_q), .Q(d_ff_2_q));  // open: Qn, preset, en, reset
  xor xor_1 (xor_1_out, d_ff_1_q, d_ff_2_q);
  and and_3 (and_3_out, d_ff_1_q, xor_1_out);
  and and_4 (and_4_out, xor_1_out, d_ff_2_q);
  and and_5 (out_2, in_1, and_3_out);
  and and_6 (out_3, in_1, and_4_out);
endmodule

module MoreMearlyCombo (
  input  in_1,
  output out_2,
  output out_3,
  output out_4,
  output out_5
);

  wire and_1_out, and_2_out, and_3_out, and_4_out, and_7_out, and_8_out, clock_1_out, d_ff_1_q, d_ff_1_qn,
       d_ff_2_q, d_ff_3_q, d_ff_3_qn, d_ff_4_q, not_1_out, not_2_out, or_1_out, or_2_out, xor_1_out,
       xor_2_out;

  Clock clock_1 (.out(clock_1_out));
  not not_1 (not_1_out, in_1);
  not not_2 (not_2_out, in_1);
  and and_1 (and_1_out, d_ff_3_qn, in_1);
  and and_2 (and_2_out, d_ff_3_q, not_1_out);
  and and_3 (and_3_out, d_ff_1_qn, in_1);
  and and_4 (and_4_out, d_ff_1_q, not_2_out);
  or or_1 (or_1_out, and_3_out, and_4_out);
  or or_2 (or_2_out, and_1_out, and_2_out);
  D_Flip_Flop d_ff_1 (.clk(clock_1_out), .D(or_1_out), .Q(d_ff_1_q), .Qn(d_ff_1_qn));  // open: preset, en, reset
  D_Flip_Flop d_ff_2 (.clk(clock_1_out), .D(d_ff_1_q), .Q(d_ff_2_q));  // open: Qn, preset, en, reset
  D_Flip_Flop d_ff_3 (.clk(clock_1_out), .D(or_2_out), .Q(d_ff_3_q), .Qn(d_ff_3_qn));  // open: preset, en, reset
  D_Flip_Flop d_ff_4 (.clk(clock_1_out), .D(d_ff_3_q), .Q(d_ff_4_q));  // open: Qn, preset, en, reset
  xor xor_1 (xor_1_out, d_ff_1_q, d_ff_2_q);
  xor xor_2 (xor_2_out, d_ff_3_q, d_ff_4_q);
  and and_5 (out_2, d_ff_1_q, xor_1_out);
  and and_6 (out_3, xor_1_out, d_ff_2_q);
  and and_7 (and_7_out, d_ff_3_q, xor_2_out);
  and and_8 (and_8_out, xor_2_out, d_ff_4_q);
  and and_9 (out_4, in_1, and_7_out);
  and and_10 (out_5, in_1, and_8_out);
endmodule
